// Logisim project Assignmenmt_1_with_ic_minimization.circ as structural Verilog: 3 circuits, main circuit main
module main (
  input  A3,
  input  A2,
  input  A1,
  input  A0,
  input  B3,
  input  B2,
  input  B1,
  input  B0,
  input  S2,
  input  S1,
  input  S0,
  output Z,
  output V,
  output C,
  output S,
  output S3,
  output out_17,
  output out_18,
  output out_19
);

  wire n7404_1_p3, n7404_1_p12, n7404_2_p3, n7404_2_p4, n7408_1_p1, n7408_1_p2, n7408_1_p4, n7408_2_p1,
       n7408_2_p2, n7408_2_p3, n7408_2_p4, n7408_2_p5, n7408_2_p6, n7408_2_p8, n7408_2_p9, n7408_2_p12,
       n7408_3_p3, n7408_3_p5, n7408_3_p6, n7408_4_p6, n7432_1_p5, n7432_1_p6, n7432_1_p9, n7432_1_p11,
       n7432_1_p12, n7432_2_p2, n7432_2_p3, n7432_2_p5, n7432_2_p6, n7432_2_p9, n7432_2_p10, n7432_2_p11,
       n7432_2_p12, n7483_corrected_2__6__s2, n7486_1_p2;

  // _7408 7408_1: pin names not known; wires that end beside it: n7408_1_p1, n7408_1_p2, n7408_1_p2, n7408_1_p4, C, V
  // _7486 7486_1: pin names not known; wires that end beside it: n7408_1_p1, n7486_1_p2, n7408_1_p4
  // _7408 7408_2: pin names not known; wires that end beside it: n7408_2_p1, n7408_2_p2, n7408_2_p3, n7408_2_p4, n7408_2_p5, n7408_2_p6, n7408_2_p5, n7408_2_p8, n7408_2_p9, n7486_1_p2, Z, n7408_2_p12
  _7483_corrected u_7483_corrected_1 (
    ._1__A4(n7432_1_p5), ._3__A3(n7408_2_p12), ._4__B3(1'b1), ._5__Vcc(1'b1), ._6__S2(n7486_1_p2),
    ._7__B2(1'b0), ._8__A2(1'b0), ._16__B4(n7432_1_p6), ._15__S4(S), ._14__Cout(n7408_1_p1),
    ._13__Cin(n7408_3_p5), ._11__B1(n7432_1_p12), ._10__A1(n7432_1_p11), ._9__S1(out_17));  // open: _2__S3, _12__GND
  // _7404 7404_1: pin names not known; wires that end beside it: S2, S1, n7404_1_p3, n7408_2_p8, out_17, B3, n7408_2_p3, n7408_2_p4, n7408_2_p2, B2, n7408_1_p2, n7404_1_p12
  // _7432 7432_1: pin names not known; wires that end beside it: n7408_2_p4, n7408_2_p6, S2, A3, n7432_1_p5, n7432_1_p6, A2, S2, n7432_1_p9, n7404_1_p12, n7432_1_p11, n7432_1_p12
  // _7408 7408_3: pin names not known; wires that end beside it: n7408_2_p8, n7408_2_p8, n7408_3_p3, S0, n7408_3_p5, n7408_3_p6, n7404_1_p12, n7404_1_p3, n7408_2_p2, S1, n7432_1_p9, n7408_2_p2
  // _7432 7432_2: pin names not known; wires that end beside it: A1, n7432_2_p2, n7432_2_p3, S2, n7432_2_p5, n7432_2_p6, A0, S2, n7432_2_p9, n7432_2_p10, n7432_2_p11, n7432_2_p12
  _7483_corrected u_7483_corrected_2 (
    ._1__A4(n7432_2_p5), ._3__A3(n7408_4_p6), ._4__B3(1'b1), ._5__Vcc(1'b1),
    ._6__S2(n7483_corrected_2__6__s2), ._7__B2(1'b0), ._8__A2(1'b0), ._16__B4(n7432_2_p6), ._15__S4(out_18),
    ._14__Cout(n7408_3_p3), ._13__Cin(n7408_3_p6), ._11__B1(n7432_2_p12), ._10__A1(n7432_2_p11),
    ._9__S1(out_19));  // open: _2__S3, _12__GND
  // _7404 7404_2: pin names not known; wires that end beside it: out_18, out_19, n7404_2_p3, n7404_2_p4, S, B1, n7408_2_p9, n7432_2_p2, B0, n7432_2_p10
  // _7408 7408_4: pin names not known; wires that end beside it: n7432_2_p11, n7483_corrected_2__6__s2, n7432_2_p2, n7408_2_p8, n7408_2_p2, n7408_4_p6, n7432_2_p3, n7404_2_p4, n7408_2_p2, n7404_2_p3, n7432_2_p10, n7408_2_p1, n7432_2_p9

  assign S3 = S;

  // Notes on the sheet:
  //   Cout
  //   s3
  //   x3
  //   y3
  //   z2
  //   y2
  //   c2
  //   s2
  //   z3
  //   x2
  //   c1
  //   s2's1
  //   y1
  //   x1
  //   s1
  //   z0
  //   B1'
  //   y0
  //   X0
  //   B0'
  //   c0
  //   z1
  //   Yi = S2+ B'
  //   Zi = s0s1'
  //   s0
  //   Xi = A + s2's1B'
endmodule

// 7483_c
module _7483_corrected (
  input  _1__A4,
  input  _16__B4,
  input  _3__A3,
  input  _4__B3,
  input  _13__Cin,
  input  _5__Vcc,
  input  _12__GND,
  input  _11__B1,
  input  _7__B2,
  input  _10__A1,
  input  _8__A2,
  output _2__S3,
  output _15__S4,
  output _14__Cout,
  output _6__S2,
  output _9__S1
);

  wire and_1_out, and_2_out, and_3_out, and_4_out, and_5_out, and_6_out, and_7_out, and_8_out, and_9_out,
       and_10_out, and_11_out, and_12_out, and_13_out, and_14_out, nand_1_out, nand_2_out, nand_3_out,
       nand_4_out, nor_1_out, nor_2_out, nor_3_out, nor_4_out, nor_6_out, nor_7_out, nor_8_out, not_1_out,
       not_2_out, not_3_out, not_4_out, not_5_out, not_6_out;

  nand nand_1 (nand_1_out, _16__B4, _1__A4);
  nor nor_1 (nor_1_out, _16__B4, _1__A4);
  nand nand_2 (nand_2_out, _4__B3, _3__A3);
  nor nor_2 (nor_2_out, _4__B3, _3__A3);
  nand nand_3 (nand_3_out, _7__B2, _8__A2);
  nor nor_3 (nor_3_out, _7__B2, _8__A2);
  nand nand_4 (nand_4_out, _11__B1, _10__A1);
  nor nor_4 (nor_4_out, _11__B1, _10__A1);
  and and_1 (and_1_out, nor_2_out, nand_1_out);
  and and_2 (and_2_out, nor_3_out, nand_1_out, nand_2_out);
  and and_3 (and_3_out, nor_4_out, nand_1_out, nand_2_out, nand_3_out);
  and and_4 (and_4_out, nand_1_out, nand_2_out, nand_3_out, nand_4_out, not_2_out);
  not not_1 (not_1_out, nor_1_out);
  and and_5 (and_5_out, nor_3_out, nand_2_out);
  and and_6 (and_6_out, nor_4_out, nand_2_out, nand_3_out);
  and and_7 (and_7_out, nand_2_out, nand_3_out, nand_4_out, not_2_out);
  not not_2 (not_2_out, _13__Cin);
  not not_3 (not_3_out, nor_2_out);
  and and_8 (and_8_out, nor_4_out, nand_3_out);
  and and_9 (and_9_out, nand_3_out, nand_4_out, not_2_out);
  not not_4 (not_4_out, nor_3_out);
  and and_10 (and_10_out, nand_4_out, not_2_out);
  not not_5 (not_5_out, nor_4_out);
  not not_6 (not_6_out, not_2_out);
  nor nor_5 (_14__Cout, nor_1_out, and_1_out, and_2_out, and_3_out, and_4_out);
  and and_11 (and_11_out, nand_1_out, not_1_out);
  and and_12 (and_12_out, nand_2_out, not_3_out);
  and and_13 (and_13_out, nand_3_out, not_4_out);
  and and_14 (and_14_out, nand_4_out, not_5_out);
  xor xor_1 (_15__S4, and_11_out, nor_6_out);
  nor nor_6 (nor_6_out, nor_2_out, and_5_out, and_6_out, and_7_out);
  xor xor_2 (_2__S3, and_12_out, nor_7_out);
  nor nor_7 (nor_7_out, nor_3_out, and_8_out, and_9_out);
  xor xor_3 (_6__S2, and_13_out, nor_8_out);
  nor nor_8 (nor_8_out, nor_4_out, and_10_out);
  xor xor_4 (_9__S1, and_14_out, not_6_out);

  // Notes on the sheet:
  //   7483: 4-bit full adder
endmodule

module test (
  input  S2,
  input  S1,
  input  S0,
  input  A3,
  input  A2,
  input  A1,
  input  A0,
  input  B3,
  input  B2,
  input  B1,
  input  B0,
  output Z,
  output V,
  output C,
  output S,
  output out_16,
  output out_17,
  output out_18,
  output out_19
);

  main main_1 (
    .Z(Z), .V(V), .C(C), .S(S), .S2(S2), .S1(S1), .S0(S0), .A3(A3), .A2(A2), .A1(A1), .A0(A0), .B3(B3),
    .B2(B2), .B1(B1), .B0(B0), .S3(out_16), .out_17(out_17), .out_18(out_18), .out_19(out_19));
endmodule
