// Logisim project Assignment_1_B1_G2.circ as structural Verilog: 5 circuits, main circuit test
module test (
  input  A3,
  input  A2,
  input  A1,
  input  A0,
  input  B3,
  input  B2,
  input  B1,
  input  B0,
  input  CS2,
  input  CS1,
  input  CS0,
  output Cout,
  output Z,
  output V,
  output S3,
  output S2,
  output S1,
  output S0
);

  ALU alu_1 (
    .Cout(Cout), .Z(Z), .V(V), .A3(A3), .A2(A2), .A1(A1), .A0(A0), .B3(B3), .B2(B2), .B1(B1), .B0(B0),
    .S3(S3), .S2(S2), .S1(S1), .S0(S0), .CS2(CS2), .CS1(CS1), .CS0(CS0));
endmodule

module ALU (
  input  CS2,
  input  CS1,
  input  CS0,
  input  A3,
  input  A2,
  input  A1,
  input  A0,
  input  B3,
  input  B2,
  input  B1,
  input  B0,
  output Cout,
  output Z,
  output V,
  output S0,
  output S3,
  output S2,
  output S1
);

  wire full_adder_2_co, full_adder_3_co, full_adder_4_co, n1bit_prepare_ckt_1_x, n1bit_prepare_ckt_1_y,
       n1bit_prepare_ckt_1_z, n1bit_prepare_ckt_2_x, n1bit_prepare_ckt_2_y, n1bit_prepare_ckt_2_z,
       n1bit_prepare_ckt_3_x, n1bit_prepare_ckt_3_y, n1bit_prepare_ckt_3_z, n1bit_prepare_ckt_4_x,
       n1bit_prepare_ckt_4_y, n1bit_prepare_ckt_4_z;

  nor nor_1 (Z, S3, S2, S1, S0);
  xor xor_1 (V, Cout, full_adder_2_co);
  _1bit_prepare_ckt u_1bit_prepare_ckt_1 (
    .S1(CS1), .S2(CS2), .A(A3), .B(B3), .X(n1bit_prepare_ckt_1_x), .Y(n1bit_prepare_ckt_1_y),
    .S0(full_adder_2_co), .Z(n1bit_prepare_ckt_1_z));
  full_adder full_adder_1 (
    .Co(Cout), .A(n1bit_prepare_ckt_1_x), .B(n1bit_prepare_ckt_1_y), .S(S3), .Ci(n1bit_prepare_ckt_1_z));
  _1bit_prepare_ckt u_1bit_prepare_ckt_2 (
    .S1(CS1), .S2(CS2), .A(A2), .B(B2), .X(n1bit_prepare_ckt_2_x), .Y(n1bit_prepare_ckt_2_y),
    .S0(full_adder_3_co), .Z(n1bit_prepare_ckt_2_z));
  full_adder full_adder_2 (
    .Co(full_adder_2_co), .A(n1bit_prepare_ckt_2_x), .B(n1bit_prepare_ckt_2_y), .S(S2),
    .Ci(n1bit_prepare_ckt_2_z));
  _1bit_prepare_ckt u_1bit_prepare_ckt_3 (
    .S1(CS1), .S2(CS2), .A(A1), .B(B1), .X(n1bit_prepare_ckt_3_x), .Y(n1bit_prepare_ckt_3_y),
    .S0(full_adder_4_co), .Z(n1bit_prepare_ckt_3_z));
  full_adder full_adder_3 (
    .Co(full_adder_3_co), .A(n1bit_prepare_ckt_3_x), .B(n1bit_prepare_ckt_3_y), .S(S1),
    .Ci(n1bit_prepare_ckt_3_z));
  _1bit_prepare_ckt u_1bit_prepare_ckt_4 (
    .S1(CS1), .S2(CS2), .A(A0), .B(B0), .X(n1bit_prepare_ckt_4_x), .Y(n1bit_prepare_ckt_4_y), .S0(CS0),
    .Z(n1bit_prepare_ckt_4_z));
  full_adder full_adder_4 (
    .Co(full_adder_4_co), .A(n1bit_prepare_ckt_4_x), .B(n1bit_prepare_ckt_4_y), .S(S0),
    .Ci(n1bit_prepare_ckt_4_z));
endmodule

// H_A
module half_adder (
  input  A,
  input  B,
  output S,
  output C
);

  xor xor_1 (S, A, B);
  and and_1 (C, A, B);
endmodule

// F_A
module full_adder (
  input  Ci,
  input  A,
  input  B,
  output Co,
  output S
);

  wire half_adder_1_c, half_adder_1_s, half_adder_2_c;

  half_adder half_adder_1 (.A(A), .B(B), .S(half_adder_1_s), .C(half_adder_1_c));
  half_adder half_adder_2 (.A(half_adder_1_s), .B(Ci), .S(S), .C(half_adder_2_c));
  or or_1 (Co, half_adder_2_c, half_adder_1_c);
endmodule

// Ckt
module _1bit_prepare_ckt (
  input  A,
  input  B,
  input  S0,
  input  S1,
  input  S2,
  output Z,
  output X,
  output Y
);

  wire and_2_out, not_1_out, not_2_out, not_3_out;

  not not_1 (not_1_out, S2);
  not not_2 (not_2_out, S1);
  and and_1 (Z, not_2_out, S0);
  and and_2 (and_2_out, not_1_out, not_3_out, S1);
  or or_1 (X, A, and_2_out);
  not not_3 (not_3_out, B);
  or or_2 (Y, S2, not_3_out);

  // Notes on the sheet:
  //   Yi = S1+ B'
  //   Zi = s0s1'
  //   Xi = A + s2's1B'
endmodule
