// Logisim project Assignment_2_B1_G2.circ as structural Verilog: 15 circuits, main circuit main
module main (
  input  A_sign,
  input  B_sign,
  input  [9:0] A_exp,
  input  [9:0] B_exp,
  input  [20:0] A_frac,
  input  [20:0] B_frac
);

  wire comparator_1_lt, comparator_2_lt, control_1_out_2, control_1_out_3;
  wire [4:0] n16_to_5_1_out_2, normal_1_shiftamount;
  wire [9:0] exp_select_1_out_3, exp_shift_1_out_4;
  wire [15:0] adder_1_out, exponent_diff_1_diff, multiplexer_1_out, n2_s_complimemnt_1_out_2;
  wire [20:0] multiplexer_2_out, multiplexer_3_out, shifter_1_out_3, shifter_2_out_3, sign_check_1_out_3,
       sign_check_2_out_3;
  wire [31:0] exp_shift_1_out_5, n21_to_32_1_out_2, n21_to_32_2_out_2, n32_bit_adder_1_s;

  Exponent_diff exponent_diff_1 (.A(A_exp), .B(B_exp), .diff(exponent_diff_1_diff));  // open: C_out
  Exp_select exp_select_1 (.A(B_exp), .B(A_exp), .out_3(exp_select_1_out_3));
  // Probe on exp_select_1_out_3
  Comparator #(.width(16)) comparator_1 (
    .a(exponent_diff_1_diff), .b({16{1'b0}}), .lt(comparator_1_lt));  // open: gt, eq
  _2_s_complimemnt u_2_s_complimemnt_1 (.in_1(exponent_diff_1_diff), .out_2(n2_s_complimemnt_1_out_2));
  Control control_1 (.in_1(exponent_diff_1_diff), .out_2(control_1_out_2), .out_3(control_1_out_3));
  Multiplexer #(.width(16), .enable("false")) multiplexer_1 (
    .in0(exponent_diff_1_diff), .in1(n2_s_complimemnt_1_out_2), .out(multiplexer_1_out), .sel(comparator_1_lt));
  Adder #(.width(16)) adder_1 (.a(multiplexer_1_out), .b(16'h1), .out(adder_1_out));  // open: cin, cout
  Multiplexer #(.width(21), .enable("false")) multiplexer_2 (
    .in0(B_frac), .in1(A_frac), .out(multiplexer_2_out), .sel(control_1_out_2));
  Multiplexer #(.width(21), .enable("false")) multiplexer_3 (
    .in0(B_frac), .in1(A_frac), .out(multiplexer_3_out), .sel(control_1_out_3));
  Comparator #(.width(16)) comparator_2 (.a(16'h20), .b(multiplexer_1_out), .lt(comparator_2_lt));  // open: gt, eq
  _16_to_5 u_16_to_5_1 (.in_1(adder_1_out), .out_2(n16_to_5_1_out_2));
  sign_check sign_check_1 (.in_1(A_sign), .in_2(shifter_1_out_3), .out_3(sign_check_1_out_3));
  shifter shifter_1 (.Number_to_be_shifted(multiplexer_3_out), .Shift_amount(5'b00001), .out_3(shifter_1_out_3));
  shifter shifter_2 (
    .Number_to_be_shifted(multiplexer_2_out), .Shift_amount(n16_to_5_1_out_2), .out_3(shifter_2_out_3));
  // Probe on sign_check_1_out_3
  _21_to_32 u_21_to_32_1 (.A(sign_check_1_out_3), .out_2(n21_to_32_1_out_2));
  _21_to_32 u_21_to_32_2 (.A(sign_check_2_out_3), .out_2(n21_to_32_2_out_2));
  sign_check sign_check_2 (.in_1(B_sign), .in_2(shifter_2_out_3), .out_3(sign_check_2_out_3));
  // Probe on n32_bit_adder_1_s
  _32_bit_adder u_32_bit_adder_1 (
    .C_in(1'b0), .A(n21_to_32_1_out_2), .B(n21_to_32_2_out_2), .S(n32_bit_adder_1_s));  // open: C_out
  normal normal_1 (.Input(n32_bit_adder_1_s), .ShiftAmount(normal_1_shiftamount));
  // Probe on normal_1_shiftamount
  exp_shift exp_shift_1 (
    .in_1(exp_select_1_out_3), .in_2(n32_bit_adder_1_s), .in_3(normal_1_shiftamount),
    .out_4(exp_shift_1_out_4), .out_5(exp_shift_1_out_5));
  // Probe on exp_shift_1_out_4
  // Probe on exp_shift_1_out_5
endmodule

module _16_bit_adder (
  input  C_in,
  input  [15:0] A,
  input  [15:0] B,
  output [15:0] out_4,
  output out_5
);

  Adder #(.width(16)) adder_1 (.a(A), .b(B), .out(out_4), .cin(C_in), .cout(out_5));
endmodule

module _32_bit_adder (
  input  C_in,
  input  [31:0] A,
  input  [31:0] B,
  output [31:0] S,
  output C_out
);

  Adder #(.width(32)) adder_1 (.a(A), .b(B), .out(S), .cin(C_in), .cout(C_out));
endmodule

// Exp_diff
module Exponent_diff (
  input  [9:0] A,
  input  [9:0] B,
  output [15:0] diff,
  output C_out
);

  wire [9:0] not_1_out;

  assign not_1_out = ~B;  // NOT_Gate not_1, 10 bits wide
  _16_bit_adder u_16_bit_adder_1 (
    .C_in(1'b1), .A({{6{1'b0}}, A}), .B({{6{1'b1}}, not_1_out}), .out_4(diff), .out_5(C_out));
endmodule

module Control (
  input  [15:0] in_1,
  output out_2,
  output out_3
);

  not not_1 (out_3, in_1[15]);

  assign out_2 = in_1[15];
endmodule

// 2's
module _2_s_complimemnt (
  input  [15:0] in_1,
  output [15:0] out_2
);

  wire subtractor_1_bout;

  Subtractor #(.width(16)) subtractor_1 (.a({16{1'b0}}), .b(in_1), .out(out_2), .bin(1'b0), .bout(subtractor_1_bout));
endmodule

module _21_to_32 (
  input  [20:0] A,
  output [31:0] out_2
);


  assign out_2 = {A, {11{1'b0}}};
endmodule

module _16_to_5 (
  input  [15:0] in_1,
  output [4:0] out_2
);


  assign out_2 = in_1[4:0];
endmodule

module trial (
  input  [9:0] in_1
);

  Comparator #(.width(10), .mode("unsigned")) comparator_1 (.a(in_1), .b({10{1'b0}}));  // open: gt, eq, lt
endmodule

module shifter (
  input  [20:0] Number_to_be_shifted,
  input  [4:0] Shift_amount,
  output [20:0] out_3
);

  wire comparator_1_eq, comparator_1_gt, or_1_out;
  wire [4:0] subtractor_1_out;
  wire [20:0] shifter_1_out, shifter_2_out;
  wire [20:20] not_1_out;

  Comparator #(.width(5)) comparator_1 (
    .a(Shift_amount), .b(5'b00001), .gt(comparator_1_gt), .eq(comparator_1_eq));  // open: lt
  or or_1 (or_1_out, comparator_1_gt, comparator_1_eq);
  Subtractor #(.width(5)) subtractor_1 (
    .a(Shift_amount), .b(5'b00001), .out(subtractor_1_out), .bin(1'b0));  // open: bout
  not not_1 (not_1_out[20], shifter_1_out[20]);
  Shifter #(.width(21), .shift("lr")) shifter_1 (.in(Number_to_be_shifted), .\dist (5'b00001), .out(shifter_1_out));
  Shifter #(.width(21), .shift("lr")) shifter_2 (
    .in({not_1_out[20], shifter_1_out[19:0]}), .\dist (subtractor_1_out), .out(shifter_2_out));
  Multiplexer #(.width(21), .enable("false")) multiplexer_1 (
    .in0(Number_to_be_shifted), .in1(shifter_2_out), .out(out_3), .sel(or_1_out));
endmodule

module Exp_select (
  input  [9:0] A,
  input  [9:0] B,
  output [9:0] out_3
);

  wire comparator_1_lt;

  Comparator #(.width(10), .mode("unsigned")) comparator_1 (.a(A), .b(B), .lt(comparator_1_lt));  // open: gt, eq
  Multiplexer #(.width(10), .enable("false")) multiplexer_1 (.in0(A), .in1(B), .out(out_3), .sel(comparator_1_lt));
endmodule

module ALU (
  input  Selection,
  input  [31:0] A,
  input  [31:0] B
);
endmodule

module sign_check (
  input  in_1,
  input  [20:0] in_2,
  output [20:0] out_3
);

  wire [20:0] subtractor_1_out;

  Subtractor #(.width(21)) subtractor_1 (.a({21{1'b0}}), .b(in_2), .out(subtractor_1_out), .bin(1'b0));  // open: bout
  Multiplexer #(.width(21), .enable("false")) multiplexer_1 (
    .in0(in_2), .in1(subtractor_1_out), .out(out_3), .sel(in_1));
endmodule

module normal (
  input  [31:0] Input,
  output [4:0] ShiftAmount
);

  wire [4:0] bitfinder_1_index;

  BitFinder #(.width(32), .\type ("high1")) bitfinder_1 (.in(Input), .index(bitfinder_1_index));  // open: found
  Subtractor #(.width(5)) subtractor_1 (
    .a({5{1'b0}}), .b(bitfinder_1_index), .out(ShiftAmount), .bin(1'b0));  // open: bout
endmodule

module exp_shift (
  input  [9:0] in_1,
  input  [31:0] in_2,
  input  [4:0] in_3,
  output [9:0] out_4,
  output [31:0] out_5
);

  Adder #(.width(10)) adder_1 (.a(in_1), .b({{5{1'b0}}, in_3}), .out(out_4), .cin(1'b0));  // open: cout
  Shifter #(.width(32)) shifter_1 (.in(in_2), .\dist (in_3), .out(out_5));
endmodule
