// Logisim project Half_adder_me.circ as structural Verilog: 3 circuits, main circuit main
module main (
  input  S0,
  input  S1,
  input  S2,
  input  Ci,
  input  A3,
  input  A2,
  input  A1,
  input  A0,
  input  B3,
  input  B2,
  input  B1,
  input  B0,
  output Co,
  output out_14,
  output out_15,
  output out_16,
  output out_17
);

  wire and_1_out, and_2_out, and_3_out, and_4_out, and_5_out, and_6_out, and_7_out, and_8_out, and_9_out,
       and_10_out, and_11_out, and_12_out, and_13_out, full_adder_2_co, full_adder_3_co, full_adder_4_co,
       not_1_out, not_2_out, not_3_out, not_4_out, not_5_out, not_6_out, or_1_out, or_2_out, or_3_out,
       or_4_out, or_5_out, or_6_out, or_7_out, or_8_out;

  not not_1 (not_1_out, S1);
  not not_2 (not_2_out, S2);
  and and_1 (and_1_out, S1, S2);
  or or_1 (or_1_out, and_1_out, and_3_out);
  and and_2 (and_2_out, S1, not_2_out, B3);
  or or_2 (or_2_out, and_2_out, A3);
  and and_3 (and_3_out, S2, not_1_out, not_3_out);
  Full_adder full_adder_1 (.Co(Co), .A(or_2_out), .B(or_1_out), .S(out_14), .Ci(and_4_out));
  and and_4 (and_4_out, full_adder_2_co, not_1_out);
  and and_5 (and_5_out, S1, not_2_out, B2);
  or or_3 (or_3_out, and_5_out, A2);
  and and_6 (and_6_out, S2, not_1_out, not_4_out);
  or or_4 (or_4_out, and_6_out, and_1_out);
  Full_adder full_adder_2 (.Co(full_adder_2_co), .A(or_3_out), .B(or_4_out), .S(out_17), .Ci(and_7_out));
  not not_3 (not_3_out, B3);
  and and_7 (and_7_out, full_adder_3_co, not_1_out);
  not not_4 (not_4_out, B2);
  not not_5 (not_5_out, B1);
  and and_8 (and_8_out, S2, not_1_out, not_5_out);
  or or_5 (or_5_out, and_1_out, and_8_out);
  Full_adder full_adder_3 (.Co(full_adder_3_co), .A(or_6_out), .B(or_5_out), .S(out_15), .Ci(and_10_out));
  not not_6 (not_6_out, B0);
  and and_9 (and_9_out, S1, not_2_out, B1);
  or or_6 (or_6_out, A1, and_9_out);
  and and_10 (and_10_out, full_adder_4_co, not_1_out);
  and and_11 (and_11_out, S2, not_1_out, not_6_out);
  and and_12 (and_12_out, S1, not_2_out, B0);
  or or_7 (or_7_out, and_12_out, A0);
  or or_8 (or_8_out, and_11_out, and_1_out);
  Full_adder full_adder_4 (.Co(full_adder_4_co), .A(or_7_out), .B(or_8_out), .S(out_16), .Ci(and_13_out));
  and and_13 (and_13_out, S0, not_1_out);
endmodule

// H_A
module Half_adder (
  input  A,
  input  B,
  output S,
  output C
);

  xor xor_1 (S, A, B);
  and and_1 (C, A, B);
endmodule

// F_A
module Full_adder (
  input  Ci,
  input  A,
  input  B,
  output Co,
  output S
);

  wire half_adder_1_c, half_adder_1_s, half_adder_2_c;

  Half_adder half_adder_1 (.A(A), .B(B), .S(half_adder_1_s), .C(half_adder_1_c));
  Half_adder half_adder_2 (.A(half_adder_1_s), .B(Ci), .S(S), .C(half_adder_2_c));
  or or_1 (Co, half_adder_2_c, half_adder_1_c);
endmodule
